// Logisim project Control Unit.circ as structural Verilog: 1 circuit, main circuit main
module main (
  input  A,
  input  B,
  input  C,
  input  D,
  output Format,
  output AL0,
  output AL1,
  output AL2,
  output In,
  output Out,
  output ResultLoad,
  output Store,
  output ResultSll,
  output Cin,
  output Binv,
  output bne,
  output jump
);

  wire and_1_out, and_2_out, and_3_out, and_4_out, and_5_out, and_6_out, and_7_out, and_8_out, and_9_out,
       and_11_out, and_12_out, and_14_out, and_15_out, and_16_out, and_17_out, not_1_out, not_2_out,
       not_3_out, not_4_out, not_5_out, not_6_out, not_7_out, not_8_out, not_9_out, not_10_out, not_11_out,
       not_12_out, not_13_out, not_14_out, not_15_out, not_16_out, not_17_out, not_18_out, not_19_out,
       not_20_out, not_21_out, not_22_out, not_23_out, not_24_out, not_25_out, not_26_out, not_27_out,
       not_28_out;

  not not_1 (not_1_out, C);
  not not_2 (not_2_out, A);
  not not_3 (not_3_out, D);
  not not_4 (not_4_out, C);
  and and_1 (and_1_out, B, not_5_out);
  not not_5 (not_5_out, D);
  not not_6 (not_6_out, B);
  not not_7 (not_7_out, C);
  and and_2 (and_2_out, not_6_out, not_7_out, not_8_out);
  not not_8 (not_8_out, D);
  not not_9 (not_9_out, A);
  and and_3 (and_3_out, not_9_out, C, D);
  not not_10 (not_10_out, A);
  and and_4 (and_4_out, not_10_out, B, D);
  not not_11 (not_11_out, B);
  and and_5 (and_5_out, not_11_out, not_12_out);
  not not_12 (not_12_out, D);
  not not_13 (not_13_out, A);
  and and_6 (and_6_out, not_13_out, B, D);
  and and_7 (and_7_out, B, C);
  and and_8 (and_8_out, A, not_14_out);
  not not_14 (not_14_out, B);
  and and_9 (and_9_out, A, not_15_out);
  not not_15 (not_15_out, D);
  not not_16 (not_16_out, B);
  not not_17 (not_17_out, C);
  not not_18 (not_18_out, B);
  not not_19 (not_19_out, D);
  and and_10 (ResultLoad, B, C, D);
  not not_20 (not_20_out, B);
  not not_21 (not_21_out, C);
  not not_22 (not_22_out, D);
  not not_23 (not_23_out, A);
  not not_24 (not_24_out, D);
  and and_11 (and_11_out, B, not_25_out);
  not not_25 (not_25_out, D);
  and and_12 (and_12_out, B, not_26_out);
  not not_26 (not_26_out, D);
  and and_13 (bne, A, C, D);
  not not_27 (not_27_out, C);
  not not_28 (not_28_out, D);
  and and_14 (and_14_out, B, not_1_out, D);
  and and_15 (and_15_out, not_2_out, B, C, not_3_out);
  and and_16 (and_16_out, A, C, D);
  and and_17 (and_17_out, A, B, not_4_out);
  or or_1 (AL0, and_1_out, A);
  or or_2 (AL1, and_2_out, and_3_out, and_4_out);
  or or_3 (AL2, and_5_out, and_6_out, and_7_out, and_8_out, and_9_out);
  and and_18 (In, A, not_16_out, not_17_out, D);
  and and_19 (Out, A, not_18_out, C, not_19_out);
  and and_20 (Store, A, not_20_out, not_21_out, not_22_out);
  and and_21 (ResultSll, not_23_out, B, C, not_24_out);
  or or_4 (Cin, and_11_out, A);
  or or_5 (Binv, and_12_out, A);
  and and_22 (jump, A, B, not_27_out, not_28_out);
  or or_6 (Format, and_14_out, and_15_out, and_16_out, and_17_out);
endmodule
