// Logisim project Input V2.circ as structural Verilog: 3 circuits, main circuit main
module main (
  input  _1,
  input  _2,
  input  _3,
  input  _4,
  input  _5,
  input  _6,
  input  in_7,
  input  _7,
  input  _8,
  input  _9,
  output [3:0] out_11
);

  wire decimal_to_bcd_1_a, decimal_to_bcd_1_b, decimal_to_bcd_1_c, decimal_to_bcd_1_d;

  Decimal_to_BCD decimal_to_bcd_1 (
    ._1(_1), ._2(_2), ._3(_3), ._4(_4), ._5(_5), ._6(_6), ._7(_7), ._8(_8), ._9(_9), ._0(1'b0),
    .A(decimal_to_bcd_1_a), .B(decimal_to_bcd_1_b), .C(decimal_to_bcd_1_c), .D(decimal_to_bcd_1_d));
  Input_Memory input_memory_1 (
    .A(decimal_to_bcd_1_a), .B(decimal_to_bcd_1_b), .C(decimal_to_bcd_1_c), .D(decimal_to_bcd_1_d),
    .A_2(out_11[0]), .B_2(out_11[1]), .C_2(out_11[2]), .D_2(out_11[3]), ._7clr(in_7));
endmodule

module Decimal_to_BCD (
  input  _1,
  input  _2,
  input  _3,
  input  _4,
  input  _5,
  input  _6,
  input  _7,
  input  _8,
  input  _9,
  input  _0,
  output A,
  output B,
  output C,
  output D
);

  or u_A (A, _1, _5, _3, _7, _9);
  or u_B (B, _2, _3, _0, _6, _7);
  or u_C (C, _4, _5, _6, _7);
  or u_D (D, _8, _0, _9);
endmodule

module Input_Memory (
  input  A,
  input  B,
  input  C,
  input  D,
  input  _7clr,
  output A_2,
  output B_2,
  output C_2,
  output D_2
);

  wire or_1_out;

  or or_1 (or_1_out, D, C, B, A);
  Register #(.width(4)) register_1 (
    .D({D, C, B, A}), .Q({D_2, C_2, B_2, A_2}), .clk(or_1_out), .clr(_7clr));  // open: en
endmodule
